// Digital circuit Processador.dig as structural Verilog
module Processador (
  input  clk
);

  wire Enable, multiplexer_1_out, SelB, SOMA_1_p3;
  wire [2:0] fun;
  wire [3:0] Mem__Programa_d, Mem__Programa_d_2, Mem__Programa_d_3, opcode, SOMA_1_p1;
  wire [11:0] Mem__Controle_d;
  wire [15:0] Mem__Programa_d_4;
  wire [31:0] multiplexer_2_out, registrador32bit_1_p1, registrador32bit_1_p7, registrador32bit_1_p8,
       sinalext_1_out;

  // ip SOMA_1: pin names not known; wires that end beside it: SOMA_1_p1, 24'h1, SOMA_1_p3
  Multiplexer multiplexer_1 (.in_0(Mem__Programa_d_4[0]), .in_1(SOMA_1_p3), .out(multiplexer_1_out));  // open: sel
  // IP___1 ip___1_1: pin names not known; wires that end beside it: multiplexer_1_out, clk, SOMA_1_p1
  ROM #(.AddrBits(4), .Bits(32)) Mem__Programa (
    .A(SOMA_1_p1), .sel(1'b1),
    .D({Mem__Programa_d_4, Mem__Programa_d_3, Mem__Programa_d_2, Mem__Programa_d, opcode}));
  ROM #(.AddrBits(4), .Bits(12)) Mem__Controle (.A(opcode), .sel(1'b1), .D(Mem__Controle_d));
  SinalEXt sinalext_1 (.In(Mem__Programa_d_4), .Out(sinalext_1_out));
  // Registrador32bit registrador32bit_1: pin names not known; wires that end beside it: registrador32bit_1_p1, Mem__Programa_d, Mem__Programa_d_2, Mem__Programa_d_3, Enable, clk, registrador32bit_1_p7, registrador32bit_1_p8
  Multiplexer #(.Bits(32)) multiplexer_2 (
    .sel(SelB), .in_0(registrador32bit_1_p8), .in_1(sinalext_1_out), .out(multiplexer_2_out));
  // Probe Display on registrador32bit_1_p7
  ULA ula_1 (.A(registrador32bit_1_p7), .B(multiplexer_2_out), .fun(fun), .G(registrador32bit_1_p1));
  // Pins of 1 and 16 bits meet at Mem__Programa_d_4

  // Notes on the sheet:
  //   O que é const?
  //   SelB, Fun e WriteEnable?
endmodule
